# Fritzing sketch laser_alarm (saved by Fritzing 0.9.3b)
breadboards: 1

parts:
  Part1 = Arduino Nano (Rev3.0)
  LED1 = LED - 5mm [color="Yellow (595nm)" package="5 mm [THT]"]
  R1 = Resistor [tolerance=±5% resistance=220 package=THT]
  Part2 = Passive Buzzer
  Mod1 = laser receiver [package=THT]
  Mod2 = laser receiver [package=THT]
  Mod3 = KY-008 Laser Transmitter Module [package="Breakout board"]
  Mod4 = KY-008 Laser Transmitter Module [package="Breakout board"]

nets:
  N1: Part1.GND, R1.Pin_0, Part2.S, Mod1.pin1, Mod2.pin1, Mod3.-, Mod4.-
  N2: Part1.D3, LED1.anode
  N3: Part1.D8, Mod1.pin2
  N4: Part1.D9, Mod2.pin2
  N5: Part1.D11/MOSI, Mod3.S
  N6: Part1.D12/MISO, Mod4.S
  N7: LED1.cathode, R1.Pin_1
  N8: Part2.GND, Mod1.pin3, Mod2.pin3, Mod3.NC, Mod4.NC

custom parts:
  laser receiver: Generic non modulated laser receiver module.
  KY-008 Laser Transmitter Module: KY-008 Laser Transmitter Module, emits a dot shaped red laser beam.
